// Logisim project bitwiseOps.circ as structural Verilog: 1 circuit, main circuit main
module main (
  input  [31:0] A,
  input  [31:0] B,
  output [31:0] AND_OUT,
  output [31:0] OR_OUT,
  output [31:0] NOT_OUT,
  output [31:0] XOR_OUT,
  output [31:0] NAND_OUT
);

  assign AND_OUT = A & B;  // AND_Gate and_1, 32 bits wide
  assign OR_OUT = A | B;  // OR_Gate or_1, 32 bits wide
  assign NOT_OUT = ~A;  // NOT_Gate not_1, 32 bits wide
  assign XOR_OUT = A ^ B;  // XOR_Gate xor_1, 32 bits wide
  assign NAND_OUT = ~(A & B);  // NAND_Gate nand_1, 32 bits wide
endmodule
